// Digital circuit 01_Complete.dig as structural Verilog
module _01_Complete (
  input  [3:0] in,
  output out
);

  wire and_1_out, and_2_out, and_3_out, and_4_out;

  and and_1 (and_1_out, in[3], in[1], ~in[0]);  // And
  and and_2 (and_2_out, ~in[3], in[2], ~in[1]);  // And
  and and_3 (and_3_out, ~in[3], ~in[2], in[0]);  // And
  and and_4 (and_4_out, ~in[1], in[0]);  // And
  or or_1 (out, and_1_out, and_2_out, and_3_out, and_4_out);
endmodule
