// Digital circuit 02_Complete.dig as structural Verilog
module _02_Complete (
  input  [2:0] in0,
  input  [2:0] in1,
  input  addsubtract,
  output [2:0] out
);

  wire and_1_out, and_2_out, and_3_out, and_4_out, and_5_out, and_6_out, and_7_out, and_8_out, and_9_out,
       and_10_out, and_11_out, and_12_out, and_13_out, and_14_out;
  wire [1:0] ip0, ip1;
  wire [2:0] oadd, osub;

  and and_1 (and_1_out, in0[2], ~in0[1], ~in0[0]);  // And
  and and_2 (and_2_out, ~in0[2], in0[1], ~in0[0]);  // And
  and and_3 (and_3_out, ~in0[2], ~in0[1], in0[0]);  // And
  and and_4 (and_4_out, in0[2], in0[1], in0[0]);
  and and_5 (and_5_out, in0[1], in0[0]);
  and and_6 (and_6_out, in0[2], in0[0]);
  and and_7 (and_7_out, in0[2], in0[1]);
  or or_1 (ip0[0], and_1_out, and_2_out, and_3_out, and_4_out);
  or or_2 (ip0[1], and_5_out, and_6_out, and_7_out);
  and and_8 (and_8_out, in1[2], ~in1[1], ~in1[0]);  // And
  and and_9 (and_9_out, ~in1[2], in1[1], ~in1[0]);  // And
  and and_10 (and_10_out, ~in1[2], ~in1[1], in1[0]);  // And
  and and_11 (and_11_out, in1[2], in1[1], in1[0]);
  and and_12 (and_12_out, in1[1], in1[0]);
  and and_13 (and_13_out, in1[2], in1[0]);
  and and_14 (and_14_out, in1[2], in1[1]);
  or or_3 (ip1[0], and_8_out, and_9_out, and_10_out, and_11_out);
  or or_4 (ip1[1], and_12_out, and_13_out, and_14_out);
  Multiplexer #(.Bits(3)) multiplexer_1 (.sel(addsubtract), .in_0(oadd), .in_1(osub), .out(out));
  Add #(.Bits(2)) add_1 (.a(ip0), .b(ip1), .c_i(1'b0), .s(oadd[1:0]), .c_o(oadd[2]));
  Sub #(.Bits(2)) sub_1 (.a(ip0), .b(ip1), .c_i(1'b0), .s(osub[1:0]), .c_o(osub[2]));

  // Other names for the same wires on the sheet: addsub = addsubtract
endmodule
