// Digital circuit 02_not-solved.dig as structural Verilog
module _02_not_solved (
  input  [2:0] in0,
  input  [2:0] in1,
  input  in_3,
  output [1:0] out_4
);

  wire and_1_out, and_2_out, and_3_out, and_4_out, and_5_out, and_6_out, and_7_out, and_8_out, and_9_out,
       and_10_out, and_11_out, and_12_out, and_13_out, and_14_out, not_1_out, not_2_out, not_3_out,
       not_4_out, not_5_out, not_6_out;
  wire [1:0] add_1_s, ip0, ip1, sub_1_s;

  not not_1 (not_1_out, in0[2]);
  not not_2 (not_2_out, in0[1]);
  not not_3 (not_3_out, in0[0]);
  and and_1 (and_1_out, in0[2], not_2_out, not_3_out);
  and and_2 (and_2_out, not_1_out, in0[1], not_3_out);
  and and_3 (and_3_out, not_1_out, not_2_out, in0[0]);
  and and_4 (and_4_out, in0[2], in0[1], in0[0]);
  and and_5 (and_5_out, in0[1], in0[0]);
  and and_6 (and_6_out, in0[2], in0[0]);
  and and_7 (and_7_out, in0[2], in0[1]);
  or or_1 (ip0[0], and_1_out, and_2_out, and_3_out, and_4_out);
  or or_2 (ip0[1], and_5_out, and_6_out, and_7_out);
  not not_4 (not_4_out, in1[2]);
  not not_5 (not_5_out, in1[1]);
  not not_6 (not_6_out, in1[0]);
  and and_8 (and_8_out, in1[2], not_5_out, not_6_out);
  and and_9 (and_9_out, not_4_out, in1[1], not_6_out);
  and and_10 (and_10_out, not_4_out, not_5_out, in1[0]);
  and and_11 (and_11_out, in1[2], in1[1], in1[0]);
  and and_12 (and_12_out, in1[1], in1[0]);
  and and_13 (and_13_out, in1[2], in1[0]);
  and and_14 (and_14_out, in1[2], in1[1]);
  or or_3 (ip1[0], and_8_out, and_9_out, and_10_out, and_11_out);
  or or_4 (ip1[1], and_12_out, and_13_out, and_14_out);
  Add #(.Bits(2)) add_1 (.a(ip0), .b(ip1), .c_i(1'b0), .s(add_1_s));  // open: c_o
  Sub #(.Bits(2)) sub_1 (.a(ip0), .b(ip1), .c_i(1'b0), .s(sub_1_s));  // open: c_o
  Multiplexer #(.Bits(2)) multiplexer_1 (.sel(in_3), .in_0(add_1_s), .in_1(sub_1_s), .out(out_4));
endmodule
