// Digital circuit DigLo66_Quiz2__01-002651.dig as structural Verilog
module DigLo66_Quiz2__01_002651 (
  input  clk,
  input  reset,
  output C,
  output B,
  output A
);

  wire and_1_out, and_2_out, and_3_out, and_4_out, and_5_out, and_6_out, and_7_out, and_8_out, and_9_out,
       not_1_out, not_2_out, not_3_out, or_1_out, or_2_out, or_3_out;

  not not_1 (not_1_out, C);
  not not_2 (not_2_out, B);
  not not_3 (not_3_out, A);
  and and_1 (and_1_out, B, not_3_out);
  and and_2 (and_2_out, C, A);
  and and_3 (and_3_out, B, not_3_out);
  and and_4 (and_4_out, not_1_out, A);
  and and_5 (and_5_out, not_1_out, not_2_out);
  and and_6 (and_6_out, C, B);
  or or_1 (or_1_out, and_1_out, and_2_out);
  or or_2 (or_2_out, and_3_out, and_4_out);
  or or_3 (or_3_out, and_5_out, and_6_out);
  and and_7 (and_7_out, ~reset, or_1_out);  // And
  and and_8 (and_8_out, ~reset, or_2_out);  // And
  and and_9 (and_9_out, ~reset, or_3_out);  // And
  D_FF d_ff_1 (.D(and_7_out), .C(clk), .Q(C));  // open: nQ
  D_FF d_ff_2 (.D(and_8_out), .C(clk), .Q(B));  // open: nQ
  D_FF d_ff_3 (.D(and_9_out), .C(clk), .Q(A));  // open: nQ

  // Other names for the same wires on the sheet: q0 = C; q1 = B; q2 = A
endmodule
