// Digital circuit Exam1_2_Complete.dig as structural Verilog
module Exam1_2_Complete (
  input  X1,
  input  X0,
  input  Y1,
  input  Y0,
  input  [1:0] in_6,
  output [4:0] Z
);

  wire [2:0] mul_2_mul;
  wire [3:0] apow2;
  wire [4:0] apow3;

  Mul #(.Bits(2)) mul_1 (.a({X1, X0}), .b({X1, X0}), .mul(apow2));
  Mul #(.Bits(4)) mul_2 (.a({in_6, X1, X0}), .b(apow2), .mul({mul_2_mul, apow3}));
  Multiplexer #(.Bits(5), .Selector_Bits(2)) multiplexer_1 (
    .sel({Y1, Y0}), .in_0(5'b00001), .in_1({3'b000, X1, X0}), .in_2({1'b0, apow2}), .in_3(apow3), .out(Z));
  // also tied to GND on the sheet: {mul_2_mul[0], mul_2_mul[1], mul_2_mul[2]}

  // Other names for the same wires on the sheet: dump[1:0] = in_6; pow2[3:0] = apow2; ix[1:0] = {X1, X0}
endmodule
