// Digital circuit Exam1_3_Complete.dig as structural Verilog
module Exam1_3_Complete (
  input  A1,
  input  A2,
  input  A3,
  input  B1,
  input  B2,
  input  B3,
  input  B4,
  output Y
);

  wire a, and_1_out, and_2_out, and_3_out, and_4_out, and_5_out, and_6_out, and_7_out, and_8_out, and_9_out,
       b;

  and and_1 (and_1_out, A3, A2);
  and and_2 (and_2_out, A3, A1);
  and and_3 (and_3_out, A2, A1);
  or or_1 (Y, a, b);
  or or_2 (a, and_1_out, and_2_out, and_3_out);
  and and_4 (and_4_out, B4, B3);
  and and_5 (and_5_out, B4, B2);
  and and_6 (and_6_out, B3, B2);
  and and_7 (and_7_out, B4, B1);
  and and_8 (and_8_out, B3, B1);
  and and_9 (and_9_out, B2, B1);
  or or_3 (b, and_4_out, and_5_out, and_6_out, and_7_out, and_8_out, and_9_out);
endmodule
