// Digital circuit Arithmetic.dig as structural Verilog
module Arithmetic (
  input  [4:0] OpCode,
  input  clk,
  input  [7:0] AccA,
  input  [7:0] AccB,
  input  Reset,
  output [7:0] Output,
  output Done,
  output Load,
  output [7:0] Output_2,
  output Done_2,
  output Load_2,
  output [7:0] Output_3,
  output Done_3,
  output Load_3,
  output Done_4,
  output Load_4,
  output Done_5,
  output Load_5,
  output Done_6,
  output gr,
  output eq,
  output ls,
  output Done_7,
  output [7:0] Output_4,
  output [7:0] Output_5,
  output [7:0] Output_6,
  output Done_8,
  output eq_2
);

  wire and_1_out, and_2_out, and_3_out, and_4_out, and_5_out, and_6_out, and_7_out, and_8_out, and_9_out,
       and_10_out, and_11_out, and_12_out, and_13_out, and_15_out, and_16_out, and_17_out, comparator_1_gt,
       comparator_2_eq, comparator_2_gt, comparator_2_lt, d_ff_5_nq, d_ff_6_nq, d_ff_7_nq, d_ff_8_nq,
       d_ff_9_nq, d_ff_9_q, d_ff_11_nq, d_ff_12_nq, d_ff_13_nq, d_ff_14_nq, d_ff_15_nq, d_ff_19_nq,
       d_ff_19_q, d_ff_20_q, d_ff_21_nq, d_ff_21_q, d_ff_23_nq, d_ff_24_nq, d_ff_28_nq, d_ff_30_nq,
       multiplexer_8_out, multiplexer_9_out, multiplexer_10_out, or_2_out, rom_1_d;
  wire [3:0] multiplexer_2_out;
  wire [7:0] add_1_s, and_14_out, barrelshifter_1_out, d_ff_1_q, d_ff_2_q, d_ff_3_q, d_ff_4_q, d_ff_10_q,
       d_ff_17_q, d_ff_18_q, d_ff_22_q, div_1_q, div_1_r, mul_1_mul, multiplexer_1_out, multiplexer_7_out,
       not_1_out, or_1_out, sub_1_s, xor_1_out;

  Comparator #(.Bits(8)) comparator_1 (.a(AccB), .b(8'h7), .gt(comparator_1_gt));  // open: eq, lt
  and and_1 (and_1_out, OpCode[4], ~OpCode[3], ~OpCode[2], ~OpCode[1], OpCode[0]);  // And
  and and_2 (and_2_out, OpCode[4], ~OpCode[3], ~OpCode[2], ~OpCode[1], OpCode[0]);  // And
  and and_3 (and_3_out, OpCode[4], ~OpCode[3], ~OpCode[2], ~OpCode[1], OpCode[0]);  // And
  Div #(.Bits(8)) div_1 (.a(AccA), .b(AccB), .q(div_1_q), .r(div_1_r));
  and and_4 (and_4_out, OpCode[4], ~OpCode[3], OpCode[2], ~OpCode[1]);  // And
  and and_5 (and_5_out, OpCode[4], OpCode[3], OpCode[2], ~OpCode[1], ~OpCode[0]);  // And
  Add #(.Bits(8)) add_1 (.a(AccA), .b(AccB), .c_i(1'b0), .s(add_1_s));  // open: c_o
  and and_6 (and_6_out, and_1_out, d_ff_11_nq, d_ff_5_nq);
  Sub #(.Bits(8)) sub_1 (.a(AccA), .b(AccB), .c_i(1'b0), .s(sub_1_s));  // open: c_o
  and and_7 (and_7_out, and_2_out, d_ff_12_nq, d_ff_6_nq);
  Mul #(.Bits(4)) mul_1 (.a(AccA[3:0]), .b(AccB[3:0]), .mul(mul_1_mul));
  and and_8 (and_8_out, and_3_out, d_ff_13_nq, d_ff_7_nq);
  Multiplexer #(.Bits(8)) multiplexer_1 (.sel(OpCode[0]), .in_0(div_1_q), .in_1(div_1_r), .out(multiplexer_1_out));
  and and_9 (and_9_out, and_4_out, d_ff_14_nq, d_ff_8_nq);
  Multiplexer #(.Bits(4)) multiplexer_2 (
    .sel(comparator_1_gt), .in_0(AccB[3:0]), .in_1(4'b0111), .out(multiplexer_2_out));
  and and_10 (and_10_out, and_5_out, d_ff_15_nq, d_ff_9_nq);
  D_FF #(.Bits(8)) d_ff_1 (.D(add_1_s), .C(clk), .Q(d_ff_1_q));  // open: nQ
  D_FF #(.Bits(8)) d_ff_2 (.D(sub_1_s), .C(clk), .Q(d_ff_2_q));  // open: nQ
  D_FF #(.Bits(8)) d_ff_3 (.D(mul_1_mul), .C(clk), .Q(d_ff_3_q));  // open: nQ
  D_FF #(.Bits(8)) d_ff_4 (.D(multiplexer_1_out), .C(clk), .Q(d_ff_4_q));  // open: nQ
  BarrelShifter #(.Bits(8), .barrelShifterMode("rotate")) barrelshifter_1 (
    .in(AccA), .shift(multiplexer_2_out), .out(barrelshifter_1_out));
  D_FF d_ff_5 (.D(and_6_out), .C(clk), .Q(Load), .nQ(d_ff_5_nq));
  D_FF d_ff_6 (.D(and_7_out), .C(clk), .Q(Load_2), .nQ(d_ff_6_nq));
  D_FF d_ff_7 (.D(and_8_out), .C(clk), .Q(Load_3), .nQ(d_ff_7_nq));
  D_FF d_ff_8 (.D(and_9_out), .C(clk), .Q(Load_4), .nQ(d_ff_8_nq));
  D_FF d_ff_9 (.D(and_10_out), .C(clk), .Q(d_ff_9_q), .nQ(d_ff_9_nq));
  Multiplexer #(.Bits(8)) multiplexer_3 (.sel(Load), .in_0({8{1'b0}}), .in_1(d_ff_1_q), .out(Output));
  Multiplexer #(.Bits(8)) multiplexer_4 (.sel(Load_2), .in_0({8{1'b0}}), .in_1(d_ff_2_q), .out(Output_2));
  Multiplexer #(.Bits(8)) multiplexer_5 (.sel(Load_3), .in_0({8{1'b0}}), .in_1(d_ff_3_q), .out(Output_3));
  Multiplexer #(.Bits(8)) multiplexer_6 (.sel(Load_4), .in_0({8{1'b0}}), .in_1(d_ff_4_q), .out(Output_5));
  D_FF #(.Bits(8)) d_ff_10 (.D(barrelshifter_1_out), .C(clk), .Q(d_ff_10_q));  // open: nQ
  D_FF d_ff_11 (.D(Load), .C(~clk), .Q(Done), .nQ(d_ff_11_nq));
  D_FF d_ff_12 (.D(Load_2), .C(~clk), .Q(Done_2), .nQ(d_ff_12_nq));
  D_FF d_ff_13 (.D(Load_3), .C(~clk), .Q(Done_3), .nQ(d_ff_13_nq));
  D_FF d_ff_14 (.D(Load_4), .C(~clk), .Q(Done_4), .nQ(d_ff_14_nq));
  D_FF d_ff_15 (.D(d_ff_9_q), .C(~clk), .Q(Done_7), .nQ(d_ff_15_nq));
  D_FF #(.Bits(8)) d_ff_16 (.D(d_ff_10_q), .C(d_ff_9_q), .Q(Output_4));  // open: nQ
  D_FF #(.Bits(8)) d_ff_17 (.D(AccB), .C(clk), .Q(d_ff_17_q));  // open: nQ
  and and_11 (and_11_out, OpCode[4], OpCode[3], OpCode[2], ~OpCode[1], OpCode[0]);  // And
  D_FF #(.Bits(8)) d_ff_18 (.D(AccA), .C(clk), .Q(d_ff_18_q));  // open: nQ
  and and_12 (and_12_out, OpCode[4], OpCode[3], ~OpCode[2]);  // And
  and and_13 (and_13_out, OpCode[4], ~OpCode[3], OpCode[2], OpCode[1], OpCode[0]);  // And
  assign not_1_out = ~d_ff_18_q;  // Not not_1, 8 bits wide
  assign and_14_out = d_ff_18_q & d_ff_17_q;  // And and_14, 8 bits wide
  assign or_1_out = d_ff_18_q | d_ff_17_q;  // Or or_1, 8 bits wide
  assign xor_1_out = d_ff_18_q ^ d_ff_17_q;  // XOr xor_1, 8 bits wide
  and and_15 (and_15_out, and_13_out, d_ff_28_nq, d_ff_19_nq);
  and and_16 (and_16_out, and_11_out, d_ff_30_nq, d_ff_21_nq);
  Multiplexer #(.Selector_Bits(2), .Bits(8)) multiplexer_7 (
    .sel(OpCode[1:0]), .in_0(not_1_out), .in_1(and_14_out), .in_2(or_1_out), .in_3(xor_1_out),
    .out(multiplexer_7_out));
  and and_17 (and_17_out, and_12_out, d_ff_24_nq, d_ff_23_nq);
  Comparator #(.Signed("true"), .Bits(8)) comparator_2 (
    .a(AccA), .b(AccB), .gt(comparator_2_gt), .eq(comparator_2_eq), .lt(comparator_2_lt));
  ROM #(.AddrBits(8)) rom_1 (.A(AccA), .sel(and_11_out), .D(rom_1_d));
  D_FF d_ff_19 (.D(and_15_out), .C(clk), .Q(d_ff_19_q), .nQ(d_ff_19_nq));
  D_FF d_ff_20 (.D(rom_1_d), .C(clk), .Q(d_ff_20_q));  // open: nQ
  D_FF d_ff_21 (.D(and_16_out), .C(clk), .Q(d_ff_21_q), .nQ(d_ff_21_nq));
  D_FF #(.Bits(8)) d_ff_22 (.D(multiplexer_7_out), .C(clk), .Q(d_ff_22_q));  // open: nQ
  D_FF d_ff_23 (.D(and_17_out), .C(clk), .Q(Load_5), .nQ(d_ff_23_nq));
  Multiplexer multiplexer_8 (.sel(Reset), .in_0(comparator_2_gt), .in_1(1'b0), .out(multiplexer_8_out));
  Multiplexer multiplexer_9 (.sel(Reset), .in_0(comparator_2_eq), .in_1(1'b0), .out(multiplexer_9_out));
  Multiplexer multiplexer_10 (.sel(Reset), .in_0(comparator_2_lt), .in_1(1'b0), .out(multiplexer_10_out));
  or or_2 (or_2_out, Reset, d_ff_19_q);
  Multiplexer #(.Bits(8)) multiplexer_11 (.sel(Load_5), .in_0({8{1'b0}}), .in_1(d_ff_22_q), .out(Output_6));
  D_FF d_ff_24 (.D(Load_5), .C(~clk), .Q(Done_5), .nQ(d_ff_24_nq));
  D_FF d_ff_25 (.D(multiplexer_8_out), .C(or_2_out), .Q(gr));  // open: nQ
  D_FF d_ff_26 (.D(multiplexer_9_out), .C(or_2_out), .Q(eq));  // open: nQ
  D_FF d_ff_27 (.D(multiplexer_10_out), .C(or_2_out), .Q(ls));  // open: nQ
  D_FF d_ff_28 (.D(d_ff_19_q), .C(~clk), .Q(Done_6), .nQ(d_ff_28_nq));
  D_FF d_ff_29 (.D(d_ff_20_q), .C(d_ff_21_q), .Q(eq_2));  // open: nQ
  D_FF d_ff_30 (.D(d_ff_21_q), .C(~clk), .Q(Done_8), .nQ(d_ff_30_nq));

  // Other names for the same wires on the sheet: A[7:0] = AccA; B[7:0] = AccB

  // Notes on the sheet:
  //   10001 accA < accA + accB
  //   10010 accA < accA - accB
  //   10011 accA < accA * accB
  //   1010X (accA < accA / accB)  (accA < accA % accB)
  //   11100 Bit Shift
  //   110XX Bitwise
  //   10111 Comp
  //   11101 Prime
  //   contents of rom_1 (hex, n*v repeats v):
  //   0,0,1,1,0,1,0,1,0,0,0,1,0,1,0,0,0,1,0,1,0,0,0,1,5*0,1,0,1,5*0
  //   ,1,0,0,0,1,0,1,0,0,0,1,5*0,1,5*0,1,0,1,5*0,1,0,0,0,1,0,1,5*0,1
  //   ,0,0,0,1,5*0,1,7*0,1,0,0,0,1,0,1,0,0,0,1,0,1,0,0,0,1,13*0,1,0,0,0
  //   ,1,5*0,1,0,1,9*0,1,0,1,5*0,1,5*0,1,0,0,0,1,5*0,1,5*0,1,0,1,9*0
  //   ,1,0,1,0,0,0,1,0,1,11*0,1,11*0,1,0,0,0,1,0,1,0,0,0,1,5*0,1,0,1
  //   ,9*0,1
endmodule
