// Digital circuit comp.dig as structural Verilog
module comp (
  input  [4:0] OpCode,
  input  clk,
  input  [7:0] AccA,
  input  [7:0] AccB,
  input  Reset,
  output Done,
  output gr,
  output eq,
  output ls,
  output Done_2,
  output eq_2
);

  wire and_1_out, and_2_out, and_3_out, and_4_out, comparator_1_eq, comparator_1_gt, comparator_1_lt,
       d_ff_1_nq, d_ff_1_q, d_ff_2_nq, d_ff_2_q, d_ff_6_nq, d_ff_8_nq, multiplexer_1_out, multiplexer_2_out,
       multiplexer_3_out, or_1_out;

  and and_1 (and_1_out, OpCode[4], ~OpCode[3], OpCode[2], OpCode[1], OpCode[0]);  // And
  and and_2 (and_2_out, OpCode[4], OpCode[3], OpCode[2], ~OpCode[1], OpCode[0]);  // And
  Comparator #(.Signed("true"), .Bits(8)) comparator_1 (
    .a(AccA), .b(AccB), .gt(comparator_1_gt), .eq(comparator_1_eq), .lt(comparator_1_lt));
  and and_3 (and_3_out, and_1_out, d_ff_6_nq, d_ff_1_nq);
  and and_4 (and_4_out, and_2_out, d_ff_8_nq, d_ff_2_nq);
  Multiplexer multiplexer_1 (.sel(Reset), .in_0(comparator_1_gt), .in_1(1'b0), .out(multiplexer_1_out));
  Multiplexer multiplexer_2 (.sel(Reset), .in_0(comparator_1_eq), .in_1(1'b0), .out(multiplexer_2_out));
  Multiplexer multiplexer_3 (.sel(Reset), .in_0(comparator_1_lt), .in_1(1'b0), .out(multiplexer_3_out));
  or or_1 (or_1_out, Reset, d_ff_1_q);
  D_FF d_ff_1 (.D(and_3_out), .C(clk), .Q(d_ff_1_q), .nQ(d_ff_1_nq));
  D_FF d_ff_2 (.D(and_4_out), .C(clk), .Q(d_ff_2_q), .nQ(d_ff_2_nq));
  D_FF d_ff_3 (.D(multiplexer_1_out), .C(or_1_out), .Q(gr));  // open: nQ
  D_FF d_ff_4 (.D(multiplexer_2_out), .C(or_1_out), .Q(eq));  // open: nQ
  D_FF d_ff_5 (.D(multiplexer_3_out), .C(or_1_out), .Q(ls));  // open: nQ
  D_FF d_ff_6 (.D(d_ff_1_q), .C(~clk), .Q(Done), .nQ(d_ff_6_nq));
  D_FF d_ff_7 (.C(d_ff_2_q), .Q(eq_2));  // open: D, nQ
  D_FF d_ff_8 (.D(d_ff_2_q), .C(~clk), .Q(Done_2), .nQ(d_ff_8_nq));

  // Other names for the same wires on the sheet: A[7:0] = AccA; B[7:0] = AccB
endmodule
