// Digital circuit final.dig as structural Verilog
module \final  (
  input  [7:0] M,
  input  [7:0] N,
  input  [12:0] progIN,
  input  reset,
  input  progLoad,
  input  start,
  input  result,
  input  clk,
  output valid,
  output done,
  output [7:0] \output ,
  output [7:0] pc,
  output [1:0] state,
  output [7:0] accA,
  output [7:0] accB,
  output [7:0] regC,
  output [7:0] ou1,
  output [7:0] out,
  output [7:0] operand,
  output [7:0] m_2,
  output [7:0] n_2,
  output [7:0] lcm1,
  output [7:0] lcm2
);

  wire _0, _1, _2, _3, _4, _5, _6, _7, _8, _9, _10, _11, _12, _13, _14, _15, _16, _17, _18, _19, _20, _21,
       _22, _23, _24, _25, _26, _27, _28, _29, _30, _31, and_1_out, and_2_out, and_3_out, and_5_out,
       and_7_out, and_8_out, and_9_out, and_10_out, and_11_out, and_12_out, and_13_out, and_14_out,
       and_16_out, and_17_out, and_18_out, and_25_out, and_26_out, and_27_out, and_28_out, and_29_out,
       and_30_out, and_31_out, and_32_out, and_33_out, and_34_out, and_35_out, and_36_out, and_37_out,
       and_38_out, and_39_out, and_40_out, and_41_out, and_42_out, and_43_out, and_44_out, and_45_out,
       and_46_out, and_47_out, and_48_out, and_49_out, and_50_out, and_51_out, and_52_out, and_53_out,
       and_54_out, and_55_out, and_56_out, and_57_out, and_58_out, and_59_out, and_60_out, and_61_out,
       and_62_out, and_63_out, and_64_out, and_65_out, and_66_out, and_67_out, and_68_out, and_69_out,
       and_70_out, and_71_out, and_72_out, and_73_out, and_74_out, and_75_out, and_76_out, and_77_out,
       and_78_out, and_79_out, and_80_out, and_81_out, and_82_out, and_83_out, and_84_out, and_85_out,
       and_86_out, and_87_out, and_88_out, and_89_out, and_90_out, and_91_out, and_92_out, and_93_out,
       and_94_out, and_95_out, and_96_out, and_97_out, and_98_out, and_99_out, and_100_out, and_101_out,
       comparator_1_lt, comparator_2_gt, comparator_4_eq, decode, driver_26_out, driver_30_out,
       driverinvsel_1_out, enableA, enableB, enableC, \end , eqflag, equal, execute, fetch, greater, grflag,
       idle, isprime, jump, leflag, lesser, ll, lll, multiplexer_4_out, multiplexer_6_out, multiplexer_7_out,
       not_2_out, not_3_out, not_4_out, not_5_out, not_6_out, not_7_out, not_8_out, not_9_out, not_10_out,
       not_11_out, not_12_out, not_13_out, not_14_out, not_15_out, not_16_out, not_17_out, not_18_out,
       not_19_out, not_20_out, not_21_out, not_22_out, not_23_out, not_24_out, not_25_out, not_26_out,
       not_27_out, not_28_out, not_29_out, not_30_out, not_31_out, not_32_out, not_33_out, not_34_out,
       not_35_out, not_36_out, not_37_out, not_38_out, not_39_out, not_40_out, not_41_out, not_42_out,
       not_43_out, not_44_out, not_45_out, not_46_out, not_47_out, not_48_out, not_49_out, not_50_out,
       not_51_out, not_52_out, not_53_out, not_54_out, not_55_out, not_56_out, or_1_out, or_2_out, or_3_out,
       or_5_out, or_6_out, or_7_out, or_8_out, or_9_out, or_10_out, or_11_out, or_12_out, or_13_out,
       or_14_out, or_15_out, or_18_out, or_19_out, or_20_out, or_21_out, or_22_out, or_23_out, or_27_out,
       or_28_out, or_29_out, or_31_out, out_t, read, resetcnt, resetting, rread;
  wire [1:0] nstate;
  wire [4:0] multiplexer_10_out, nopcode, opcode;
  wire [7:0] acnt, add_1_s, and_6_out, barrelshifter_1_out, cnt, counter_1_out, div_1_q, div_1_r, Expo,
       mul_1_mul, multiplexer_1_out, multiplexer_2_out, multiplexer_8_out, multiplexer_9_out,
       multiplexer_11_out, multiplexer_12_out, multiplexer_13_out, multiplexer_14_out, multiplexer_15_out,
       multiplexer_16_out, multiplexer_17_out, multiplexer_18_out, multiplexer_19_out, multiplexer_20_out,
       ncnt, not_1_out, npc, nrcnt, or_4_out, rAddress, rcnt, rom_1_d, rom_1_d_2, scnt, sub_1_s, toaccA,
       toaccB, toregC, xor_1_out;
  wire [12:0] Din;

  and and_1 (and_1_out, enableA, execute);
  and and_2 (and_2_out, enableB, execute);
  and and_3 (and_3_out, enableC, execute);
  or or_1 (or_1_out, and_1_out, reset);
  or or_2 (or_2_out, and_2_out, reset);
  or or_3 (or_3_out, and_3_out, reset);
  Register #(.Bits(8)) u_accA (.D(toaccA), .C(clk), .en(or_1_out), .Q(accA));
  Register #(.Bits(8)) u_accB (.D(toaccB), .C(clk), .en(or_2_out), .Q(accB));
  Register #(.Bits(8)) u_RegC (.D(toregC), .C(clk), .en(or_3_out), .Q(regC));
  and and_4 (lll, ~nopcode[0], nopcode[1], nopcode[2], nopcode[3], nopcode[4]);  // And
  assign toaccB = _2 ? operand : 8'bz;  // Driver driver_1
  assign toaccB = _4 ? accA : 8'bz;  // Driver driver_2
  assign toaccB = reset ? {8{1'b0}} : 8'bz;  // Driver driver_3
  Div #(.Bits(8)) div_1 (.a(accA), .b(accB), .q(div_1_q), .r(div_1_r));
  Comparator #(.Bits(8)) comparator_1 (.a(rcnt), .b(8'hf), .lt(comparator_1_lt));  // open: gt, eq
  Comparator #(.Bits(8)) comparator_2 (.a(cnt), .b({8{1'b0}}), .gt(comparator_2_gt), .eq(resetcnt));  // open: lt
  Add #(.Bits(8)) add_1 (.a(accA), .b(accB), .c_i(1'b0), .s(add_1_s));  // open: c_o
  Sub #(.Bits(8)) sub_1 (.a(accA), .b(accB), .c_i(1'b0), .s(sub_1_s));  // open: c_o
  Mul #(.Bits(4)) mul_1 (.a(accA[3:0]), .b(accB[3:0]), .mul(mul_1_mul));
  and and_5 (and_5_out, resetcnt, resetting);
  assign not_1_out = ~accA;  // Not not_1, 8 bits wide
  assign and_6_out = accA & accB;  // And and_6, 8 bits wide
  assign or_4_out = accA | accB;  // Or or_4, 8 bits wide
  assign xor_1_out = accA ^ accB;  // XOr xor_1, 8 bits wide
  BarrelShifter #(.Bits(8)) barrelshifter_1 (.in(accA), .shift({1'b0, accB[2:0]}), .out(barrelshifter_1_out));
  or or_5 (or_5_out, progLoad, start);
  Multiplexer #(.Bits(8)) multiplexer_1 (.sel(read), .in_0(pc), .in_1(operand), .out(multiplexer_1_out));
  or or_6 (or_6_out, comparator_1_lt, comparator_2_gt);
  assign toaccA = _1 ? operand : 8'bz;  // Driver driver_4
  assign toaccA = _3 ? accB : 8'bz;  // Driver driver_5
  assign toaccA = _6 ? regC : 8'bz;  // Driver driver_6
  assign toaccA = _9 ? {n_2[3:0], m_2[3:0]} : 8'bz;  // Driver driver_7
  assign toaccA = _10 ? out : 8'bz;  // Driver driver_8
  assign toaccA = _17 ? add_1_s : 8'bz;  // Driver driver_9
  assign toaccA = _18 ? sub_1_s : 8'bz;  // Driver driver_10
  assign toaccA = reset ? {8{1'b0}} : 8'bz;  // Driver driver_11
  assign toaccA = _19 ? mul_1_mul : 8'bz;  // Driver driver_12
  assign toaccA = _20 ? div_1_q : 8'bz;  // Driver driver_13
  assign toaccA = _21 ? div_1_r : 8'bz;  // Driver driver_14
  assign toaccA = _24 ? not_1_out : 8'bz;  // Driver driver_15
  assign toaccA = _25 ? and_6_out : 8'bz;  // Driver driver_16
  assign toaccA = _26 ? or_4_out : 8'bz;  // Driver driver_17
  assign toaccA = _27 ? xor_1_out : 8'bz;  // Driver driver_18
  assign toaccA = _28 ? barrelshifter_1_out : 8'bz;  // Driver driver_19
  assign toaccA = _22 ? Expo : 8'bz;  // Driver driver_20
  Multiplexer #(.Bits(8)) multiplexer_2 (.sel(or_7_out), .in_0(ncnt), .in_1({8{1'b0}}), .out(multiplexer_2_out));
  or or_7 (or_7_out, and_5_out, start);
  and and_7 (and_7_out, resetting, or_6_out);
  Register #(.Bits(8)) register_1 (.D(multiplexer_2_out), .C(clk), .en(or_5_out), .Q(cnt));
  RAMDualAccess #(.AddrBits(8), .Bits(13)) pRAM (
    .str(progLoad), .C(clk), .ld(1'b1), .A1(cnt), .Din1(Din), .A2(multiplexer_1_out),
    .D2({nopcode, n_2[3:0], m_2[3:0]}));  // open: D1
  Multiplexer #(.Bits(13)) multiplexer_3 (.sel(resetting), .in_0(progIN), .in_1({13{1'b0}}), .out(Din));
  or or_8 (or_8_out, reset, and_7_out);
  not not_2 (not_2_out, isprime);
  D_FF d_ff_1 (.D(or_8_out), .C(clk), .Q(resetting));  // open: nQ
  or or_9 (or_9_out, eqflag, grflag);
  Comparator #(.Signed("true"), .Bits(8)) comparator_3 (.a(accA), .b(accB), .gt(greater), .eq(equal), .lt(lesser));
  or or_10 (or_10_out, reset, not_2_out);
  and and_8 (and_8_out, _13, eqflag);
  and and_9 (and_9_out, _14, grflag);
  and and_10 (and_10_out, _15, leflag);
  and and_11 (and_11_out, _16, or_9_out);
  Multiplexer multiplexer_4 (.sel(or_10_out), .in_0(equal), .in_1(1'b0), .out(multiplexer_4_out));
  or or_11 (or_11_out, _23, _29);
  or or_12 (or_12_out, _9, _10);
  or or_13 (or_13_out, decode, execute);
  and and_12 (and_12_out, execute, _23);
  or or_14 (or_14_out, and_12_out, reset);
  and and_13 (and_13_out, execute, _23);
  or or_15 (or_15_out, isprime, multiplexer_4_out);
  and and_14 (and_14_out, execute, or_11_out);
  or or_16 (rread, out_t, read);
  Multiplexer #(.Bits(8)) multiplexer_5 (.sel(resetting), .in_0(acnt), .in_1(scnt), .out(ncnt));
  or or_17 (jump, _12, and_8_out, and_9_out, and_10_out, and_11_out);
  Multiplexer multiplexer_6 (.sel(reset), .in_0(greater), .in_1(1'b0), .out(multiplexer_6_out));
  Multiplexer multiplexer_7 (.sel(reset), .in_0(lesser), .in_1(1'b0), .out(multiplexer_7_out));
  or or_18 (or_18_out, and_13_out, reset);
  or or_19 (or_19_out, and_14_out, reset);
  Sub #(.Bits(8)) sub_2 (.a(cnt), .b(8'h1), .c_i(1'b0), .s(scnt));  // open: c_o
  and and_15 (read, or_12_out, or_13_out);
  Register u_GrFlag (.D(multiplexer_6_out), .C(clk), .en(or_14_out), .Q(grflag));
  Register u_LeFlag (.D(multiplexer_7_out), .C(clk), .en(or_18_out), .Q(leflag));
  Register u_EqFlag (.D(or_15_out), .C(clk), .en(or_19_out), .Q(eqflag));
  Add #(.Bits(8)) add_2 (.a(cnt), .b(8'h1), .c_i(1'b0), .s(acnt));  // open: c_o
  Multiplexer #(.Bits(8)) multiplexer_8 (.sel(fetch), .in_0(8'he), .in_1({4'b0000, m_2[3:0]}), .out(multiplexer_8_out));
  assign toregC = _5 ? accA : 8'bz;  // Driver driver_21
  assign toregC = _7 ? M : 8'bz;  // Driver driver_22
  assign toregC = _8 ? N : 8'bz;  // Driver driver_23
  Multiplexer #(.Bits(8)) multiplexer_9 (.sel(execute), .in_0(multiplexer_8_out), .in_1(8'hf), .out(multiplexer_9_out));
  Multiplexer #(.Bits(5)) multiplexer_10 (.sel(valid), .in_0(nopcode), .in_1({5{1'b0}}), .out(multiplexer_10_out));
  Multiplexer #(.Bits(8)) multiplexer_11 (.sel(execute), .in_0(lcm1), .in_1(lcm2), .out(multiplexer_11_out));
  Multiplexer #(.Bits(8)) multiplexer_12 (.sel(resetting), .in_0({8{1'b0}}), .in_1(nrcnt), .out(multiplexer_12_out));
  or or_20 (or_20_out, resetting, reset);
  or or_21 (or_21_out, fetch, \end );
  assign toregC = reset ? {8{1'b0}} : 8'bz;  // Driver driver_24
  ROM #(.AddrBits(16), .Bits(16)) rom_1 (.A({ou1, out}), .sel(lll), .D({rom_1_d_2, rom_1_d}));
  Multiplexer #(.Bits(8)) multiplexer_13 (
    .sel(lll), .in_0(operand), .in_1(multiplexer_9_out), .out(multiplexer_13_out));
  Register #(.Bits(8)) register_2 (.D(multiplexer_12_out), .C(clk), .en(or_20_out), .Q(rcnt));
  Register #(.Bits(5)) register_3 (.D(multiplexer_10_out), .C(clk), .en(or_21_out), .Q(opcode));
  Register #(.Bits(8)) register_4 (.D({n_2[3:0], m_2[3:0]}), .C(clk), .en(fetch), .Q(operand));
  Multiplexer #(.Bits(8)) multiplexer_14 (
    .sel(resetting), .in_0(multiplexer_13_out), .in_1(rcnt), .out(multiplexer_14_out));
  Multiplexer #(.Bits(8)) multiplexer_15 (.sel(lll), .in_0(accA), .in_1(multiplexer_11_out), .out(multiplexer_15_out));
  Multiplexer #(.Bits(8)) multiplexer_16 (
    .sel(resetting), .in_0(multiplexer_15_out), .in_1({8{1'b0}}), .out(multiplexer_16_out));
  and and_16 (and_16_out, fetch, lll);
  and and_17 (and_17_out, fetch, lll);
  and and_18 (and_18_out, _11, execute);
  or or_22 (or_22_out, and_18_out, ll, resetting);
  Multiplexer #(.Bits(8)) multiplexer_17 (
    .sel(or_23_out), .in_0(rAddress), .in_1(multiplexer_18_out), .out(multiplexer_17_out));
  Decoder #(.Selector_Bits(5)) decoder_1 (
    .sel(opcode), .out_0(_0), .out_1(_1), .out_2(_2), .out_3(_3), .out_4(_4), .out_5(_5), .out_6(_6),
    .out_7(_7), .out_8(_8), .out_9(_9), .out_10(_10), .out_11(_11), .out_12(_12), .out_13(_13), .out_14(_14),
    .out_15(_15), .out_16(_16), .out_17(_17), .out_18(_18), .out_19(_19), .out_20(_20), .out_21(_21),
    .out_22(_22), .out_23(_23), .out_24(_24), .out_25(_25), .out_26(_26), .out_27(_27), .out_28(_28),
    .out_29(_29), .out_30(_30), .out_31(_31));
  Register #(.Bits(8)) register_5 (.D(rom_1_d_2), .C(clk), .en(and_16_out), .Q(lcm1));
  Register #(.Bits(8)) register_6 (.D(rom_1_d), .C(clk), .en(and_17_out), .Q(lcm2));
  RAMDualAccess #(.AddrBits(8), .Bits(8)) rRAM (
    .str(or_22_out), .C(clk), .ld(1'b1), .A1(multiplexer_14_out), .Din1(multiplexer_16_out),
    .A2(multiplexer_17_out), .D1(ou1), .D2(out));
  Multiplexer #(.Bits(8)) multiplexer_18 (
    .sel(lll), .in_0(operand), .in_1({4'b0000, n_2[3:0]}), .out(multiplexer_18_out));
  Sub #(.Bits(8)) sub_3 (.a(counter_1_out), .b(8'h1), .c_i(1'b0), .s(rAddress));  // open: c_o
  or or_23 (or_23_out, read, lll);
  Add #(.Bits(8)) add_3 (.a(rcnt), .b(8'h1), .c_i(1'b0), .s(nrcnt));  // open: c_o
  Add #(.Bits(8)) add_4 (.a(pc), .b(8'h1), .c_i(1'b0), .s(npc));  // open: c_o
  Counter #(.Bits(8)) counter_1 (.en(out_t), .C(clk), .clr(comparator_4_eq), .out(counter_1_out));  // open: ovf
  assign driverinvsel_1_out = ~done ? out_t : 1'bz;  // DriverInvSel driverinvsel_1
  PullDown pulldown_1 (.out(driverinvsel_1_out));
  assign driverinvsel_1_out = result ? 1'b1 : 1'bz;  // Driver driver_25
  or or_24 (enableA, _1, _3, _6, _9, _10, _17, _18, _19, _20, _21, _22, _28, _24, _25, _26, _27);
  or or_25 (enableB, _2, _4);
  or or_26 (enableC, _5, _7, _8);
  and and_19 (out_t, 1'b1, driverinvsel_1_out);
  Comparator #(.Bits(8)) comparator_4 (.a(counter_1_out), .b(8'h10), .eq(comparator_4_eq));  // open: gt, lt
  D_FF #(.Bits(2)) d_ff_2 (.D(nstate), .C(clk), .Q(state));  // open: nQ
  Comparator #(.Bits(5)) comparator_5 (.a(opcode), .b({5{1'b1}}), .eq(\end ));  // open: gt, lt
  not not_3 (not_3_out, result);
  or or_27 (or_27_out, reset, start, comparator_4_eq, result);
  or or_28 (or_28_out, execute, decode);
  assign driver_26_out = result ? not_3_out : 1'bz;  // Driver driver_26
  assign driver_26_out = comparator_4_eq ? comparator_4_eq : 1'bz;  // Driver driver_27
  Register register_7 (.D(driver_26_out), .C(clk), .en(or_27_out), .Q(done));
  and and_20 (ll, or_28_out, _30);
  assign driver_26_out = reset ? not_4_out : 1'bz;  // Driver driver_28
  assign driver_26_out = start ? not_5_out : 1'bz;  // Driver driver_29
  Multiplexer #(.Bits(8)) multiplexer_19 (.sel(jump), .in_0(npc), .in_1(operand), .out(multiplexer_19_out));
  not not_4 (not_4_out, reset);
  not not_5 (not_5_out, start);
  Multiplexer #(.Bits(8)) multiplexer_20 (
    .sel(idle), .in_0(multiplexer_19_out), .in_1({8{1'b0}}), .out(multiplexer_20_out));
  or or_29 (or_29_out, execute, idle);
  not not_6 (not_6_out, state[0]);
  not not_7 (not_7_out, state[1]);
  not not_8 (not_8_out, state[0]);
  not not_9 (not_9_out, state[1]);
  and and_21 (execute, state[0], state[1]);
  and and_22 (decode, not_6_out, state[1]);
  and and_23 (fetch, state[0], not_7_out);
  and and_24 (idle, not_8_out, not_9_out);
  Register #(.Bits(8)) register_8 (.D(multiplexer_20_out), .C(clk), .en(or_29_out), .Q(pc));
  not not_10 (not_10_out, state[1]);
  not not_11 (not_11_out, \end );
  not not_12 (not_12_out, reset);
  not not_13 (not_13_out, state[0]);
  not not_14 (not_14_out, state[1]);
  not not_15 (not_15_out, \end );
  not not_16 (not_16_out, reset);
  and and_25 (and_25_out, not_10_out, state[0], not_11_out, not_12_out);
  and and_26 (and_26_out, not_13_out, not_14_out, start);
  and and_27 (and_27_out, state[1], not_15_out, not_16_out);
  not not_17 (not_17_out, reset);
  not not_18 (not_18_out, start);
  and and_28 (and_28_out, state[1], ~state[0], ~\end , ~reset);  // And
  or or_30 (nstate[0], and_26_out, and_27_out);
  assign driver_30_out = reset ? not_17_out : 1'bz;  // Driver driver_30
  assign driver_30_out = start ? not_18_out : 1'bz;  // Driver driver_31
  or or_31 (or_31_out, reset, start, \end );
  or or_32 (nstate[1], and_25_out, and_28_out);
  assign driver_30_out = \end  ? \end  : 1'bz;  // Driver driver_32
  Register register_9 (.D(driver_30_out), .C(clk), .en(or_31_out), .Q(valid));
  Seven_Seg_Hex seven_seg_hex_1 (.d(out[7:4]), .dp(1'b0));
  Seven_Seg_Hex seven_seg_hex_2 (.d(cnt[7:4]), .dp(1'b0));
  Seven_Seg_Hex seven_seg_hex_3 (.d(out[3:0]), .dp(1'b0));
  Seven_Seg_Hex seven_seg_hex_4 (.d(cnt[3:0]), .dp(1'b0));
  Seven_Seg_Hex seven_seg_hex_5 (.d(opcode[3:0]), .dp(1'b0));
  not not_19 (not_19_out, accA[7]);
  not not_20 (not_20_out, accA[6]);
  not not_21 (not_21_out, accA[5]);
  not not_22 (not_22_out, accA[4]);
  not not_23 (not_23_out, accA[3]);
  not not_24 (not_24_out, accA[2]);
  not not_25 (not_25_out, accA[1]);
  and and_29 (and_29_out, not_19_out, accA[6], accA[5], not_23_out, not_24_out, not_25_out, accA[0]);
  and and_30 (and_30_out, not_19_out, not_20_out, not_21_out, accA[4], accA[2], accA[1], accA[0]);
  and and_31 (and_31_out, not_19_out, accA[6], not_22_out, not_23_out, accA[2], accA[1], accA[0]);
  and and_32 (and_32_out, not_19_out, not_20_out, accA[4], accA[3], accA[2], not_25_out, accA[0]);
  and and_33 (and_33_out, not_19_out, accA[5], not_22_out, not_23_out, accA[2], not_25_out, accA[0]);
  and and_34 (and_34_out, accA[7], not_20_out, not_21_out, accA[4], accA[2], not_25_out, accA[0]);
  and and_35 (and_35_out, not_19_out, not_20_out, not_21_out, not_22_out, accA[2], not_25_out, accA[0]);
  and and_36 (and_36_out, not_19_out, not_21_out, not_22_out, not_23_out, accA[1], accA[0]);
  and and_37 (and_37_out, not_19_out, not_20_out, not_21_out, not_22_out, not_23_out, not_24_out, accA[1]);
  and and_38 (and_38_out, accA[7], accA[6], accA[5], accA[4], accA[3], not_24_out, accA[1], accA[0]);
  and and_39 (and_39_out, accA[7], accA[6], accA[5], not_22_out, accA[3], not_24_out, not_25_out, accA[0]);
  and and_40 (and_40_out, not_19_out, accA[6], not_21_out, accA[3], not_24_out, not_25_out, accA[0]);
  and and_41 (and_41_out, accA[7], accA[6], not_21_out, accA[4], accA[3], accA[2], accA[1], accA[0]);
  and and_42 (and_42_out, accA[7], not_20_out, accA[5], accA[4], accA[3], accA[2], accA[1], accA[0]);
  and and_43 (and_43_out, not_19_out, accA[6], accA[5], accA[4], accA[3], accA[2], accA[1], accA[0]);
  and and_44 (and_44_out, accA[7], accA[6], not_21_out, not_22_out, not_23_out, not_25_out, accA[0]);
  and and_45 (and_45_out, accA[7], not_20_out, not_21_out, not_22_out, accA[3], not_24_out, accA[0]);
  and and_46 (and_46_out, accA[7], not_20_out, accA[5], not_22_out, accA[3], accA[2], not_25_out, accA[0]);
  and and_47 (and_47_out, accA[7], not_20_out, accA[5], not_23_out, not_24_out, accA[1], accA[0]);
  and and_48 (and_48_out, accA[7], accA[6], accA[5], not_22_out, accA[3], accA[2], accA[1], accA[0]);
  and and_49 (and_49_out, not_19_out, accA[6], accA[5], not_22_out, accA[2], not_25_out, accA[0]);
  and and_50 (and_50_out, not_19_out, not_20_out, accA[5], accA[3], not_24_out, accA[1], accA[0]);
  and and_51 (and_51_out, not_19_out, not_20_out, not_21_out, accA[4], not_23_out, not_24_out, accA[0]);
  and and_52 (and_52_out, accA[7], accA[5], not_22_out, not_23_out, not_24_out, accA[1], accA[0]);
  and and_53 (and_53_out, not_19_out, not_20_out, accA[5], not_22_out, accA[3], not_24_out, accA[0]);
  and and_54 (and_54_out, not_19_out, accA[5], not_22_out, accA[3], not_24_out, accA[1], accA[0]);
  and and_55 (and_55_out, not_19_out, accA[6], not_21_out, not_22_out, accA[2], accA[1], accA[0]);
  and and_56 (and_56_out, accA[7], not_20_out, accA[5], not_22_out, not_23_out, accA[1], accA[0]);
  and and_57 (and_57_out, not_19_out, not_20_out, accA[5], not_22_out, accA[3], accA[1], accA[0]);
  and and_58 (and_58_out, accA[6], accA[5], not_22_out, not_23_out, accA[2], not_25_out, accA[0]);
  and and_59 (and_59_out, accA[6], not_21_out, not_22_out, not_23_out, accA[2], accA[1], accA[0]);
  and and_60 (and_60_out, not_20_out, accA[5], accA[4], not_23_out, accA[2], not_25_out, accA[0]);
  and and_61 (and_61_out, not_20_out, not_21_out, not_22_out, not_24_out, accA[1], accA[0]);
  and and_62 (and_62_out, not_20_out, not_21_out, accA[4], not_23_out, accA[2], accA[1], accA[0]);
  and and_63 (and_63_out, accA[6], accA[5], accA[4], not_23_out, not_24_out, not_25_out, accA[0]);
  and and_64 (and_64_out, accA[6], not_21_out, accA[4], not_23_out, not_24_out, accA[1], accA[0]);
  or or_33 (isprime, and_29_out, and_30_out, and_31_out, and_32_out, and_33_out, and_34_out, and_35_out, and_36_out, and_37_out, and_38_out, and_39_out, and_40_out, and_41_out, and_42_out, and_43_out, and_44_out, and_45_out, and_46_out, and_47_out, and_48_out, and_49_out, and_50_out, and_51_out, and_52_out, and_53_out, and_54_out, and_55_out, and_56_out, and_57_out, and_58_out, and_59_out, and_60_out, and_61_out, and_62_out, and_63_out, and_64_out);
  not not_26 (not_26_out, accA[0]);
  not not_27 (not_27_out, accB[2]);
  and and_65 (and_65_out, accA[2], accA[1], not_26_out, not_27_out, accB[1], accB[0]);
  and and_66 (and_66_out, accA[1], accA[0], accB[2], accB[1]);
  and and_67 (and_67_out, accA[1], accB[2], accB[1], accB[0]);
  and and_68 (and_68_out, accA[1], accA[0], accB[2], accB[0]);
  or or_34 (Expo[7], and_65_out, and_66_out, and_67_out, and_68_out);
  not not_28 (not_28_out, accA[2]);
  not not_29 (not_29_out, accA[0]);
  not not_30 (not_30_out, accB[2]);
  not not_31 (not_31_out, accB[1]);
  not not_32 (not_32_out, accB[0]);
  and and_69 (and_69_out, accA[2], accA[1], not_29_out, accB[2], not_31_out, accB[0]);
  and and_70 (and_70_out, not_28_out, accA[1], accA[0], accB[2], not_31_out);
  and and_71 (and_71_out, accA[2], accA[0], accB[2], not_31_out, not_32_out);
  and and_72 (and_72_out, not_28_out, accA[1], accA[0], accB[2], not_32_out);
  and and_73 (and_73_out, accA[2], accA[1], accA[0], accB[1], accB[0]);
  and and_74 (and_74_out, accA[2], not_30_out, accB[1], accB[0]);
  and and_75 (and_75_out, accA[1], not_29_out, accB[2], accB[1], not_32_out);
  or or_35 (Expo[6], and_69_out, and_70_out, and_71_out, and_72_out, and_73_out, and_74_out, and_75_out);
  not not_33 (not_33_out, accA[1]);
  not not_34 (not_34_out, accB[2]);
  not not_35 (not_35_out, accB[1]);
  not not_36 (not_36_out, accB[1]);
  and and_76 (and_76_out, accA[2], not_33_out, accA[0], not_34_out, accB[1], accB[1]);
  and and_77 (and_77_out, accA[2], accA[0], accB[2], not_35_out, not_36_out);
  and and_78 (and_78_out, accA[2], accA[1], not_34_out, accB[1], not_36_out);
  and and_79 (and_79_out, accA[2], accA[0], accB[2], accB[1]);
  and and_80 (and_80_out, accA[1], accB[2], not_35_out, accB[1]);
  or or_36 (Expo[5], and_76_out, and_77_out, and_78_out, and_79_out, and_80_out);
  not not_37 (not_37_out, accA[2]);
  not not_38 (not_38_out, accA[1]);
  not not_39 (not_39_out, accA[0]);
  not not_40 (not_40_out, accB[2]);
  not not_41 (not_41_out, accB[1]);
  not not_42 (not_42_out, accB[0]);
  and and_81 (and_81_out, not_37_out, accA[1], accA[0], accB[2], not_41_out);
  and and_82 (and_82_out, accA[2], not_38_out, not_40_out, accB[1], not_42_out);
  and and_83 (and_83_out, accA[2], not_38_out, accA[0], accB[2], not_41_out);
  and and_84 (and_84_out, accA[2], accA[1], not_39_out, not_40_out, accB[1], accB[0]);
  and and_85 (and_85_out, accA[2], not_38_out, accA[0], not_40_out, accB[1], accB[0]);
  and and_86 (and_86_out, not_37_out, accA[1], accA[0], accB[2], not_42_out);
  and and_87 (and_87_out, accA[2], accA[1], accA[0], accB[1]);
  and and_88 (and_88_out, accA[1], not_39_out, accB[2], not_41_out, not_42_out);
  and and_89 (and_89_out, accA[1], accA[0], not_40_out, accB[1], accB[0]);
  or or_37 (Expo[4], and_81_out, and_82_out, and_83_out, and_84_out, and_85_out, and_86_out, and_87_out, and_88_out, and_89_out);
  not not_43 (not_43_out, accA[2]);
  not not_44 (not_44_out, accA[1]);
  not not_45 (not_45_out, accA[0]);
  not not_46 (not_46_out, accB[2]);
  and and_90 (and_90_out, accA[2], not_44_out, accA[0], accB[1]);
  and and_91 (and_91_out, not_43_out, accA[1], accA[0], accB[1]);
  and and_92 (and_92_out, accA[1], not_45_out, not_46_out, accB[1], accB[0]);
  or or_38 (Expo[3], and_90_out, and_91_out, and_92_out);
  not not_47 (not_47_out, accA[1]);
  not not_48 (not_48_out, accA[0]);
  not not_49 (not_49_out, accB[2]);
  not not_50 (not_50_out, accB[1]);
  not not_51 (not_51_out, accB[0]);
  and and_93 (and_93_out, accA[2], not_47_out, accA[0], not_49_out, accB[1], accB[0]);
  and and_94 (and_94_out, accA[2], not_49_out, not_50_out, accB[0]);
  and and_95 (and_95_out, accA[2], accA[1], accA[0], accB[1], accB[0]);
  and and_96 (and_96_out, accA[2], accA[0], accB[2], accB[0]);
  and and_97 (and_97_out, accA[1], not_48_out, not_49_out, accB[1], not_51_out);
  or or_39 (Expo[2], and_93_out, and_94_out, and_95_out, and_96_out, and_97_out);
  not not_52 (not_52_out, accB[2]);
  not not_53 (not_53_out, accB[1]);
  and and_98 (and_98_out, accA[1], not_52_out, not_53_out, accB[0]);
  and and_99 (and_99_out, accA[1], accA[0], not_52_out, accB[1], accB[0]);
  and and_100 (and_100_out, accA[1], accA[0], accB[2], accB[0]);
  or or_40 (Expo[1], and_98_out, and_99_out, and_100_out);
  not not_54 (not_54_out, accB[2]);
  not not_55 (not_55_out, accB[1]);
  not not_56 (not_56_out, accB[0]);
  and and_101 (and_101_out, not_54_out, not_55_out, not_56_out);
  or or_41 (Expo[0], accA[0], and_101_out);

  assign m_2[7:4] = 4'b0000;
  assign n_2[7:4] = 4'b0000;
  assign \output  = out;

  // Other names for the same wires on the sheet: Done_rRam = done; output1[7:0] = ou1; m_t[3:0] = m_2[3:0];
  //   noperand[7:0] = {n_2[3:0], m_2[3:0]}; prog[12:0] = {nopcode, n_2[3:0], m_2[3:0]}; n_t[3:0] = n_2[3:0]

  // Notes on the sheet:
  //   6733273321 สิรณัฏฐ์ สิงหทัศน์(หลัก)
  //   6733017021กันณพงศ์ วังกระแสร์(หลัก)
  //   6733198021 ภาณุพงษ์ สภานนท์
  //   6733080521 ทักษ์ดนัย พรหมขจร
  //   contents of rom_1 (hex, n*v repeats v):
  //   257*0,1,2,3,4,5,6,7,8,9,a,b,c,d,e,f,10,11,12,13,14,15,16,17,18
  //   ,19,1a,1b,1c,1d,1e,1f,20,21,22,23,24,25,26,27,28,29,2a,2b,2c,2d
  //   ,2e,2f,30,31,32,33,34,35,36,37,38,39,3a,3b,3c,3d,3e,3f,40,41,42
  //   ,43,44,45,46,47,48,49,4a,4b,4c,4d,4e,4f,50,51,52,53,54,55,56,57
  //   ,58,59,5a,5b,5c,5d,5e,5f,60,61,62,63,64,65,66,67,68,69,6a,6b,6c
  //   ,6d,6e,6f,70,71,72,73,74,75,76,77,78,79,7a,7b,7c,7d,7e,7f,80,81
  //   ,82,83,84,85,86,87,88,89,8a,8b,8c,8d,8e,8f,90,91,92,93,94,95,96
  //   ,97,98,99,9a,9b,9c,9d,9e,9f,a0,a1,a2,a3,a4,a5,a6,a7,a8,a9,aa,ab
  //   ,ac,ad,ae,af,b0,b1,b2,b3,b4,b5,b6,b7,b8,b9,ba,bb,bc,bd,be,bf,c0
  //   ,c1,c2,c3,c4,c5,c6,c7,c8,c9,ca,cb,cc,cd,ce,cf,d0,d1,d2,d3,d4,d5
  //   ,d6,d7,d8,d9,da,db,dc,dd,de,df,e0,e1,e2,e3,e4,e5,e6,e7,e8,e9,ea
  //   ,eb,ec,ed,ee,ef,f0,f1,f2,f3,f4,f5,f6,f7,f8,f9,fa,fb,fc,fd,fe,ff
  //   ,0,2,2,6,4,a,6,e,8,12,a,16,c,1a,e,1e,10,22,12,26,14,2a,16,2e,18
  //   ,32,1a,36,1c,3a,1e,3e,20,42,22,46,24,4a,26,4e,28,52,2a,56,2c,5a
  //   ,2e,5e,30,62,32,66,34,6a,36,6e,38,72,3a,76,3c,7a,3e,7e,40,82,42
  //   ,86,44,8a,46,8e,48,92,4a,96,4c,9a,4e,9e,50,a2,52,a6,54,aa,56,ae
  //   ,58,b2,5a,b6,5c,ba,5e,be,60,c2,62,c6,64,ca,66,ce,68,d2,6a,d6,6c
  //   ,da,6e,de,70,e2,72,e6,74,ea,76,ee,78,f2,7a,f6,7c,fa,7e,fe,80,102
  //   ,82,106,84,10a,86,10e,88,112,8a,116,8c,11a,8e,11e,90,122,92,126
  //   ,94,12a,96,12e,98,132,9a,136,9c,13a,9e,13e,a0,142,a2,146,a4,14a
  //   ,a6,14e,a8,152,aa,156,ac,15a,ae,15e,b0,162,b2,166,b4,16a,b6,16e
  //   ,b8,172,ba,176,bc,17a,be,17e,c0,182,c2,186,c4,18a,c6,18e,c8,192
  //   ,ca,196,cc,19a,ce,19e,d0,1a2,d2,1a6,d4,1aa,d6,1ae,d8,1b2,da,1b6
  //   ,dc,1ba,de,1be,e0,1c2,e2,1c6,e4,1ca,e6,1ce,e8,1d2,ea,1d6,ec,1da
  //   ,ee,1de,f0,1e2,f2,1e6,f4,1ea,f6,1ee,f8,1f2,fa,1f6,fc,1fa,fe,1fe
  //   ,0,3,6,3,c,f,6,15,18,9,1e,21,c,27,2a,f,30,33,12,39,3c,15,42,45
  //   ,18,4b,4e,1b,54,57,1e,5d,60,21,66,69,24,6f,72,27,78,7b,2a,81,84
  //   ,2d,8a,8d,30,93,96,33,9c,9f,36,a5,a8,39,ae,b1,3c,b7,ba,3f,c0,c3
  //   ,42,c9,cc,45,d2,d5,48,db,de,4b,e4,e7,4e,ed,f0,51,f6,f9,54,ff,102
  //   ,57,108,10b,5a,111,114,5d,11a,11d,60,123,126,63,12c,12f,66,135
  //   ,138,69,13e,141,6c,147,14a,6f,150,153,72,159,15c,75,162,165,78
  //   ,16b,16e,7b,174,177,7e,17d,180,81,186,189,84,18f,192,87,198,19b
  //   ,8a,1a1,1a4,8d,1aa,1ad,90,1b3,1b6,93,1bc,1bf,96,1c5,1c8,99,1ce
  //   ,1d1,9c,1d7,1da,9f,1e0,1e3,a2,1e9,1ec,a5,1f2,1f5,a8,1fb,1fe,ab
  //   ,204,207,ae,20d,210,b1,216,219,b4,21f,222,b7,228,22b,ba,231,234
  //   ,bd,23a,23d,c0,243,246,c3,24c,24f,c6,255,258,c9,25e,261,cc,267
  //   ,26a,cf,270,273,d2,279,27c,d5,282,285,d8,28b,28e,db,294,297,de
  //   ,29d,2a0,e1,2a6,2a9,e4,2af,2b2,e7,2b8,2bb,ea,2c1,2c4,ed,2ca,2cd
  //   ,f0,2d3,2d6,f3,2dc,2df,f6,2e5,2e8,f9,2ee,2f1,fc,2f7,2fa,ff,0,4,4
  //   ,c,4,14,c,1c,8,24,14,2c,c,34,1c,3c,10,44,24,4c,14,54,2c,5c,18
  //   ,64,34,6c,1c,74,3c,7c,20,84,44,8c,24,94,4c,9c,28,a4,54,ac,2c,b4
  //   ,5c,bc,30,c4,64,cc,34,d4,6c,dc,38,e4,74,ec,3c,f4,7c,fc,40,104
  //   ,84,10c,44,114,8c,11c,48,124,94,12c,4c,134,9c,13c,50,144,a4,14c
  //   ,54,154,ac,15c,58,164,b4,16c,5c,174,bc,17c,60,184,c4,18c,64,194
  //   ,cc,19c,68,1a4,d4,1ac,6c,1b4,dc,1bc,70,1c4,e4,1cc,74,1d4,ec,1dc
  //   ,78,1e4,f4,1ec,7c,1f4,fc,1fc,80,204,104,20c,84,214,10c,21c,88
  //   ,224,114,22c,8c,234,11c,23c,90,244,124,24c,94,254,12c,25c,98,264
  //   ,134,26c,9c,274,13c,27c,a0,284,144,28c,a4,294,14c,29c,a8,2a4,154
  //   ,2ac,ac,2b4,15c,2bc,b0,2c4,164,2cc,b4,2d4,16c,2dc,b8,2e4,174,2ec
  //   ,bc,2f4,17c,2fc,c0,304,184,30c,c4,314,18c,31c,c8,324,194,32c,cc
  //   ,334,19c,33c,d0,344,1a4,34c,d4,354,1ac,35c,d8,364,1b4,36c,dc,374
  //   ,1bc,37c,e0,384,1c4,38c,e4,394,1cc,39c,e8,3a4,1d4,3ac,ec,3b4,1dc
  //   ,3bc,f0,3c4,1e4,3cc,f4,3d4,1ec,3dc,f8,3e4,1f4,3ec,fc,3f4,1fc,3fc
  //   ,0,5,a,f,14,5,1e,23,28,2d,a,37,3c,41,46,f,50,55,5a,5f,14,69,6e
  //   ,73,78,19,82,87,8c,91,1e,9b,a0,a5,aa,23,b4,b9,be,c3,28,cd,d2,d7
  //   ,dc,2d,e6,eb,f0,f5,32,ff,104,109,10e,37,118,11d,122,127,3c,131
  //   ,136,13b,140,41,14a,14f,154,159,46,163,168,16d,172,4b,17c,181
  //   ,186,18b,50,195,19a,19f,1a4,55,1ae,1b3,1b8,1bd,5a,1c7,1cc,1d1
  //   ,1d6,5f,1e0,1e5,1ea,1ef,64,1f9,1fe,203,208,69,212,217,21c,221
  //   ,6e,22b,230,235,23a,73,244,249,24e,253,78,25d,262,267,26c,7d,276
  //   ,27b,280,285,82,28f,294,299,29e,87,2a8,2ad,2b2,2b7,8c,2c1,2c6
  //   ,2cb,2d0,91,2da,2df,2e4,2e9,96,2f3,2f8,2fd,302,9b,30c,311,316
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endmodule

/* Test case 01_P01T01:
M N progIN reset progLoad start result clk valid done output
0 0 0 0 0 0 0 0 x x x
0 0 0 0 0 0 0 1 x x x
0 0 0 1 0 0 0 0 x x x
0 0 0 1 0 0 0 1 0 0 x
0 0 0 0 0 0 0 0 0 0 x
0 0 0 0 0 0 0 1 0 0 x
0 0 0 0 0 0 0 0 0 0 x
0 0 0 0 0 0 0 1 0 0 x
0 0 0 0 0 0 0 0 0 0 x
0 0 0 0 0 0 0 1 0 0 x
0 0 0 0 0 0 0 0 0 0 x
0 0 0 0 0 0 0 1 0 0 x
0 0 0 0 0 0 0 0 0 0 x
0 0 0 0 0 0 0 1 0 0 x
0 0 0 0 0 0 0 0 0 0 x
0 0 0 0 0 0 0 1 0 0 x
0 0 0 0 0 0 0 0 0 0 x
0 0 0 0 0 0 0 1 0 0 x
0 0 0 0 0 0 0 0 0 0 x
0 0 0 0 0 0 0 1 0 0 x
0 0 0 0 0 0 0 0 0 0 x
0 0 0 0 0 0 0 1 0 0 x
0 0 0 0 0 0 0 0 0 0 x
0 0 0 0 0 0 0 1 0 0 x
0 0 0 0 0 0 0 0 0 0 x
0 0 0 0 0 0 0 1 0 0 x
0 0 0 0 0 0 0 0 0 0 x
0 0 0 0 0 0 0 1 0 0 x
0 0 0 0 0 0 0 0 0 0 x
0 0 0 0 0 0 0 1 0 0 x
0 0 0 0 0 0 0 0 0 0 x
0 0 0 0 0 0 0 1 0 0 x
0 0 0 0 0 0 0 0 0 0 x
0 0 0 0 0 0 0 1 0 0 x
0 0 0 0 0 0 0 0 0 0 x
0 0 0 0 0 0 0 1 0 0 x
0 0 0 0 0 0 0 0 0 0 x
0 0 0 0 0 0 0 1 0 0 x
0 0 0 0 0 0 0 0 0 0 x
0 0 0 0 0 0 0 1 0 0 x
0 0 0 0 0 0 0 0 0 0 x
0 0 0 0 0 0 0 1 0 0 x
0 0 446 0 1 0 0 0 0 0 x
0 0 446 0 1 0 0 1 0 0 x
0 0 2817 0 1 0 0 0 0 0 x
0 0 2817 0 1 0 0 1 0 0 x
0 0 426 0 1 0 0 0 0 0 x
0 0 426 0 1 0 0 1 0 0 x
0 0 2831 0 1 0 0 0 0 0 x
0 0 2831 0 1 0 0 1 0 0 x
0 0 7711 0 1 0 0 0 0 0 x
0 0 7711 0 1 0 0 1 0 0 x
0 0 7936 0 1 0 0 0 0 0 x
0 0 7936 0 1 0 0 1 0 0 x
0 0 0 0 0 0 0 0 0 0 x
0 0 0 0 0 0 0 1 0 0 x
0 0 0 0 0 0 0 0 0 0 x
0 0 0 0 0 0 0 1 0 0 x
0 0 0 0 0 0 0 0 0 0 x
0 0 0 0 0 0 0 1 0 0 x
0 0 0 0 0 1 0 0 x 0 x
0 0 0 0 0 1 0 1 x 0 x
0 0 0 0 0 0 0 0 x 0 x
0 0 0 0 0 0 0 1 x 0 x
0 0 0 0 0 0 0 0 x 0 x
0 0 0 0 0 0 0 1 x 0 x
0 0 0 0 0 0 0 0 x 0 x
0 0 0 0 0 0 0 1 x 0 x
0 0 0 0 0 0 0 0 x 0 x
0 0 0 0 0 0 0 1 x 0 x
0 0 0 0 0 0 0 0 x 0 x
0 0 0 0 0 0 0 1 x 0 x
0 0 0 0 0 0 0 0 x 0 x
0 0 0 0 0 0 0 1 x 0 x
0 0 0 0 0 0 0 0 x 0 x
0 0 0 0 0 0 0 1 x 0 x
0 0 0 0 0 0 0 0 x 0 x
0 0 0 0 0 0 0 1 x 0 x
0 0 0 0 0 0 0 0 x 0 x
0 0 0 0 0 0 0 1 x 0 x
0 0 0 0 0 0 0 0 x 0 x
0 0 0 0 0 0 0 1 x 0 x
0 0 0 0 0 0 0 0 x 0 x
0 0 0 0 0 0 0 1 x 0 x
0 0 0 0 0 0 0 0 x 0 x
0 0 0 0 0 0 0 1 x 0 x
0 0 0 0 0 0 0 0 x 0 x
0 0 0 0 0 0 0 1 x 0 x
0 0 0 0 0 0 0 0 x 0 x
0 0 0 0 0 0 0 1 x 0 x
0 0 0 0 0 0 0 0 x 0 x
0 0 0 0 0 0 0 1 x 0 x
0 0 0 0 0 0 0 0 x 0 x
0 0 0 0 0 0 0 1 x 0 x
0 0 0 0 0 0 0 0 x 0 x
0 0 0 0 0 0 0 1 x 0 x
0 0 0 0 0 0 0 0 x 0 x
0 0 0 0 0 0 0 1 x 0 x
0 0 0 0 0 0 0 0 x 0 x
0 0 0 0 0 0 0 1 x 0 x
0 0 0 0 0 0 0 0 x 0 x
0 0 0 0 0 0 0 1 x 0 x
0 0 0 0 0 0 0 0 x 0 x
0 0 0 0 0 0 0 1 x 0 x
0 0 0 0 0 0 0 0 x 0 x
0 0 0 0 0 0 0 1 x 0 x
0 0 0 0 0 0 0 0 x 0 x
0 0 0 0 0 0 0 1 x 0 x
0 0 0 0 0 0 0 0 x 0 x
0 0 0 0 0 0 0 1 x 0 x
0 0 0 0 0 0 0 0 x 0 x
0 0 0 0 0 0 0 1 x 0 x
0 0 0 0 0 0 0 0 x 0 x
0 0 0 0 0 0 0 1 x 0 x
0 0 0 0 0 0 0 0 x 0 x
0 0 0 0 0 0 0 1 x 0 x
0 0 0 0 0 0 0 0 x 0 x
0 0 0 0 0 0 0 1 x 0 x
0 0 0 0 0 0 0 0 x 0 x
0 0 0 0 0 0 0 1 x 0 x
0 0 0 0 0 0 0 0 x 0 x
0 0 0 0 0 0 0 1 x 0 x
0 0 0 0 0 0 0 0 x 0 x
0 0 0 0 0 0 0 1 x 0 x
0 0 0 0 0 0 0 0 x 0 x
0 0 0 0 0 0 0 1 x 0 x
0 0 0 0 0 0 0 0 x 0 x
0 0 0 0 0 0 0 1 x 0 x
0 0 0 0 0 0 0 0 x 0 x
0 0 0 0 0 0 0 1 x 0 x
0 0 0 0 0 0 0 0 x 0 x
0 0 0 0 0 0 0 1 x 0 x
0 0 0 0 0 0 0 0 x 0 x
0 0 0 0 0 0 0 1 x 0 x
0 0 0 0 0 0 0 0 x 0 x
0 0 0 0 0 0 0 1 x 0 x
0 0 0 0 0 0 0 0 x 0 x
0 0 0 0 0 0 0 1 x 0 x
0 0 0 0 0 0 0 0 x 0 x
0 0 0 0 0 0 0 1 x 0 x
0 0 0 0 0 0 0 0 x 0 x
0 0 0 0 0 0 0 1 x 0 x
0 0 0 0 0 0 0 0 x 0 x
0 0 0 0 0 0 0 1 x 0 x
0 0 0 0 0 0 0 0 x 0 x
0 0 0 0 0 0 0 1 x 0 x
0 0 0 0 0 0 0 0 x 0 x
0 0 0 0 0 0 0 1 x 0 x
0 0 0 0 0 0 0 0 x 0 x
0 0 0 0 0 0 0 1 x 0 x
0 0 0 0 0 0 0 0 x 0 x
0 0 0 0 0 0 0 1 x 0 x
0 0 0 0 0 0 0 0 x 0 x
0 0 0 0 0 0 0 1 x 0 x
0 0 0 0 0 0 0 0 x 0 x
0 0 0 0 0 0 0 1 x 0 x
0 0 0 0 0 0 0 0 x 0 x
0 0 0 0 0 0 0 1 x 0 x
0 0 0 0 0 0 0 0 x 0 x
0 0 0 0 0 0 0 1 x 0 x
0 0 0 0 0 0 0 0 x 0 x
0 0 0 0 0 0 0 1 x 0 x
0 0 0 0 0 0 0 0 x 0 x
0 0 0 0 0 0 0 1 x 0 x
0 0 0 0 0 0 0 0 x 0 x
0 0 0 0 0 0 0 1 x 0 x
0 0 0 0 0 0 0 0 x 0 x
0 0 0 0 0 0 0 1 x 0 x
0 0 0 0 0 0 0 0 x 0 x
0 0 0 0 0 0 0 1 x 0 x
0 0 0 0 0 0 0 0 x 0 x
0 0 0 0 0 0 0 1 x 0 x
0 0 0 0 0 0 0 0 x 0 x
0 0 0 0 0 0 0 1 x 0 x
0 0 0 0 0 0 0 0 x 0 x
0 0 0 0 0 0 0 1 x 0 x
0 0 0 0 0 0 0 0 x 0 x
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*/
