// Digital circuit 02_Complete.dig as structural Verilog
module _02_Complete (
  input  A,
  input  B,
  output And,
  output Or,
  output Nand,
  output Nor,
  output Xor,
  output Xnor
);

  and and_1 (And, A, B);
  or or_1 (Or, A, B);
  nand nand_1 (Nand, A, B);
  nor nor_1 (Nor, A, B);
  xor xor_1 (Xor, A, B);
  xnor xnor_1 (Xnor, A, B);

  // Other names for the same wires on the sheet: _1 = A; _2 = B
endmodule
