// Digital circuit 09_Complete.dig as structural Verilog
module _09_Complete (
  input  X0,
  input  X1,
  input  S1,
  input  X2,
  input  X3,
  input  S0,
  output Z
);

  wire multiplexer_1_out, multiplexer_2_out;

  Multiplexer multiplexer_1 (.sel(S1), .in_0(X0), .in_1(X2), .out(multiplexer_1_out));
  Multiplexer multiplexer_2 (.sel(S1), .in_0(X1), .in_1(X3), .out(multiplexer_2_out));
  Multiplexer multiplexer_3 (.sel(S0), .in_0(multiplexer_1_out), .in_1(multiplexer_2_out), .out(Z));
endmodule
