// Digital circuit 09_Complete2.dig as structural Verilog
module _09_Complete2 (
  input  X0,
  input  X1,
  input  S1,
  input  X2,
  input  X3,
  input  S0,
  output Z
);

  wire and_1_out, and_2_out, n1, not_2_out, not_3_out, not_4_out, not_5_out, not_6_out, or_1_out, or_2_out,
       or_3_out, or_4_out, or_5_out, or_6_out, or_7_out, or_8_out, or_9_out;

  not not_1 (n1, S0);
  not not_2 (not_2_out, S1);
  not not_3 (not_3_out, X3);
  not not_4 (not_4_out, X2);
  not not_5 (not_5_out, X1);
  not not_6 (not_6_out, X0);
  or or_1 (or_1_out, X2, not_2_out);
  or or_2 (or_2_out, X2, X0);
  or or_3 (or_3_out, X0, S1);
  or or_4 (or_4_out, X3, not_2_out);
  or or_5 (or_5_out, X3, X1);
  or or_6 (or_6_out, X1, S1);
  and and_1 (and_1_out, or_1_out, or_2_out, or_3_out);
  and and_2 (and_2_out, or_4_out, or_5_out, or_6_out);
  or or_7 (or_7_out, and_2_out, n1);
  or or_8 (or_8_out, and_2_out, and_1_out);
  or or_9 (or_9_out, and_1_out, S0);
  and and_3 (Z, or_7_out, or_8_out, or_9_out);

  // Other names for the same wires on the sheet: _1 = S0
endmodule
