// Digital circuit 1-Complete.dig as structural Verilog
module _1_Complete (
  input  [3:0] In,
  output A,
  output B,
  output C,
  output D,
  output E,
  output F,
  output G
);

  wire and_1_out, and_2_out, and_3_out, and_4_out, and_5_out, and_6_out, and_7_out, and_8_out, and_9_out,
       and_10_out, and_11_out, and_12_out, and_13_out, and_14_out, and_15_out, and_16_out, and_17_out,
       and_18_out, and_19_out, and_20_out, and_21_out, and_22_out, and_23_out, and_24_out, and_25_out,
       not_1_out, not_2_out, not_3_out, not_4_out;

  not not_1 (not_1_out, In[3]);
  not not_2 (not_2_out, In[2]);
  not not_3 (not_3_out, In[1]);
  not not_4 (not_4_out, In[0]);
  and and_1 (and_1_out, not_2_out, not_3_out, not_4_out);
  and and_2 (and_2_out, In[3], not_2_out, not_3_out);
  and and_3 (and_3_out, not_1_out, In[1]);
  and and_4 (and_4_out, not_1_out, In[2], In[0]);
  and and_5 (and_5_out, not_1_out, In[1], In[0]);
  and and_6 (and_6_out, not_2_out, not_3_out);
  and and_7 (and_7_out, not_1_out, not_3_out, not_4_out);
  and and_8 (and_8_out, not_1_out, not_2_out);
  and and_9 (and_9_out, not_2_out, not_3_out);
  and and_10 (and_10_out, not_1_out, In[2]);
  and and_11 (and_11_out, not_1_out, In[0]);
  and and_12 (and_12_out, not_2_out, not_3_out, not_4_out);
  and and_13 (and_13_out, not_1_out, In[1], not_4_out);
  and and_14 (and_14_out, not_2_out, not_3_out, not_4_out);
  and and_15 (and_15_out, In[3], not_2_out, not_3_out);
  and and_16 (and_16_out, not_1_out, In[2]);
  and and_17 (and_17_out, not_1_out, In[1], not_4_out);
  and and_18 (and_18_out, In[3], not_2_out, not_3_out);
  and and_19 (and_19_out, not_1_out, In[2], not_3_out);
  and and_20 (and_20_out, not_1_out, not_2_out, In[1]);
  or or_1 (A, and_1_out, and_2_out, and_3_out, and_4_out);
  or or_2 (B, and_5_out, and_6_out, and_7_out, and_8_out);
  or or_3 (C, and_9_out, and_10_out, and_11_out);
  or or_4 (E, and_12_out, and_13_out);
  or or_5 (F, and_14_out, and_15_out, and_16_out);
  or or_6 (G, and_17_out, and_18_out, and_19_out, and_20_out);
  and and_21 (and_21_out, not_2_out, not_3_out, not_4_out);
  and and_22 (and_22_out, not_1_out, In[1], not_4_out);
  and and_23 (and_23_out, In[3], not_2_out, not_3_out);
  and and_24 (and_24_out, not_1_out, In[2], not_3_out, In[0]);
  and and_25 (and_25_out, not_1_out, not_2_out, In[1]);
  Seven_Seg seven_seg_1 (.a(A), .b(B), .c(C), .d(D), .e(E), .f(F), .g(G), .dp(1'b0));
  or or_7 (D, and_21_out, and_22_out, and_23_out, and_24_out, and_25_out);

  // Other names for the same wires on the sheet: ia = In[0]; ib = In[1]; ic = In[2]; id = In[3]
endmodule
