// Digital circuit Template-01.dig as structural Verilog
module Template_01 (
  input  [3:0] In,
  input  [1:0] Selector,
  output [3:0] Output
);

  wire and_1_out, and_2_out, and_3_out, and_4_out, and_5_out, and_6_out, and_7_out, and_8_out, and_9_out,
       and_10_out, and_11_out, and_12_out, and_13_out, and_14_out, and_15_out, and_16_out, and_17_out,
       not_1_out, not_2_out, not_3_out, not_4_out, not_5_out, not_6_out, not_7_out, not_8_out, not_9_out;
  wire [2:0] cyc;
  wire [3:0] ex_3, multiplexer_1_out, multiplexer_2_out;
  wire [3:1] _24c, _64c;

  not not_1 (not_1_out, In[2]);
  not not_2 (not_2_out, In[1]);
  not not_3 (not_3_out, In[2]);
  not not_4 (not_4_out, In[0]);
  not not_5 (not_5_out, In[1]);
  or or_1 (cyc[2], In[2], In[3]);
  and and_1 (and_1_out, In[1], not_1_out);
  and and_2 (and_2_out, not_2_out, In[2]);
  and and_3 (and_3_out, In[0], not_2_out);
  and and_4 (and_4_out, not_4_out, In[1]);
  not not_6 (not_6_out, In[0]);
  and and_5 (and_5_out, In[0], In[2]);
  and and_6 (and_6_out, In[1], In[2]);
  and and_7 (and_7_out, not_6_out, In[2]);
  and and_8 (and_8_out, In[1], In[2]);
  and and_9 (and_9_out, In[0], not_5_out, In[2]);
  and and_10 (and_10_out, In[1], not_3_out);
  or or_2 (cyc[1], and_1_out, and_2_out);
  or or_3 (cyc[0], and_3_out, and_4_out);
  or or_4 (_24c[3], and_5_out, and_6_out, In[3]);
  or or_5 (_24c[2], and_7_out, and_8_out, In[3]);
  or or_6 (_24c[1], and_9_out, and_10_out, In[3]);
  Add #(.Bits(4)) add_1 (.a(In), .b(4'b0011), .c_i(1'b0), .s(ex_3));  // open: c_o
  Multiplexer #(.Bits(4)) multiplexer_1 (.sel(Selector[0]), .in_0(ex_3), .in_1({In[3], cyc}), .out(multiplexer_1_out));
  Multiplexer #(.Bits(4)) multiplexer_2 (
    .sel(Selector[0]), .in_0({_24c, In[0]}), .in_1({_64c, In[0]}), .out(multiplexer_2_out));
  Multiplexer #(.Bits(4)) multiplexer_3 (
    .sel(Selector[1]), .in_0(multiplexer_1_out), .in_1(multiplexer_2_out), .out(Output));
  not not_7 (not_7_out, In[2]);
  not not_8 (not_8_out, In[1]);
  not not_9 (not_9_out, In[0]);
  and and_11 (and_11_out, In[0], In[1]);
  and and_12 (and_12_out, In[0], In[2]);
  and and_13 (and_13_out, In[0], not_8_out, not_7_out);
  and and_14 (and_14_out, not_9_out, In[2]);
  and and_15 (and_15_out, In[1], In[2]);
  and and_16 (and_16_out, not_9_out, In[1]);
  and and_17 (and_17_out, In[0], not_8_out, In[2]);
  or or_7 (_64c[3], and_11_out, and_12_out, In[3]);
  or or_8 (_64c[2], and_13_out, and_14_out, and_15_out);
  or or_9 (_64c[1], and_16_out, and_17_out, In[3]);

  // Other names for the same wires on the sheet: _24c[0] = In[0]; _64c[0] = In[0]; inp[3:0] = In; Output_00 = In[0];
  //   Output_000 = In[0]; cyc[3] = In[3]; Output_3 = In[3]; Output_0 = cyc[0]; Output_1 = cyc[1]; Output_2 = cyc[2];
  //   Output_11 = _24c[1]; Output_22 = _24c[2]; Output_33 = _24c[3]; Output_111 = _64c[1]; Output_222 = _64c[2];
  //   Output_333 = _64c[3]
endmodule
