// Digital circuit Template-02 (1).dig as structural Verilog
module Template_02__1 (
  input  [6:0] In,
  output [6:0] Output
);

  wire [2:0] xor_4_out;
  wire [6:0] ham;

  assign Output = In ^ ham;  // XOr xor_1, 7 bits wide
  xor xor_2 (xor_4_out[2], In[3], In[2], In[1], In[0]);
  xor xor_3 (xor_4_out[1], In[5], In[4], In[1], In[0]);
  xor xor_4 (xor_4_out[0], In[6], In[4], In[2], In[0]);
  Demultiplexer #(.Selector_Bits(3)) demultiplexer_1 (
    .sel(xor_4_out), .in(1'b1), .out_1(ham[6]), .out_2(ham[5]), .out_3(ham[4]), .out_4(ham[3]),
    .out_5(ham[2]), .out_6(ham[1]), .out_7(ham[0]));  // open: out_0
endmodule
