// Digital circuit 01_Complete.dig as structural Verilog
module _01_Complete (
  input  Load,
  input  A,
  output Z
);

  wire not_1_out;

  not not_1 (not_1_out, Load);
  assign Z = ~not_1_out ? A : 1'bz;  // DriverInvSel driverinvsel_1
  assign Z = ~Load ? Z : 1'bz;  // DriverInvSel driverinvsel_2
endmodule
