// Digital circuit 02_Complete.dig as structural Verilog
module _02_Complete (
  input  R,
  input  S,
  input  clk,
  output Q,
  output Q_2
);

  wire and_1_out, and_2_out;

  and and_1 (and_1_out, R, clk);
  and and_2 (and_2_out, clk, S);
  nor nor_1 (Q, and_1_out, Q_2);
  nor nor_2 (Q_2, Q, and_2_out);
endmodule
