// Digital circuit Template.dig as structural Verilog
module Template (
  input  J,
  input  K,
  input  Clear,
  input  Clock,
  output Q,
  output Q_2
);

  // And and_1 has open pins: In_1=open, In_2=K, In_3=open, out=open
endmodule
