// Digital circuit 7_Complete.dig as structural Verilog
module _7_Complete (
  input  reset,
  input  clk,
  output A,
  output B,
  output C
);

  wire and_1_out, and_2_out, and_3_out, and_4_out, and_5_out, or_1_out;

  and and_1 (and_1_out, B, ~C);  // And
  and and_2 (and_2_out, ~A, ~C);  // And
  or or_1 (or_1_out, ~B, and_2_out);  // Or
  and and_3 (and_3_out, ~reset, and_1_out);  // And
  and and_4 (and_4_out, ~reset, or_1_out);  // And
  and and_5 (and_5_out, ~reset, A);  // And
  D_FF Q0 (.D(and_3_out), .C(clk), .Q(A));  // open: nQ
  D_FF Q1 (.D(and_4_out), .C(clk), .Q(B));  // open: nQ
  D_FF Q2 (.D(and_5_out), .C(clk), .Q(C));  // open: nQ

  // Other names for the same wires on the sheet: q0 = A; q1 = B; q2 = C
endmodule
