// Digital circuit gcd_Complete.dig as structural Verilog
module gcd_Complete (
  input  [7:0] A,
  input  [7:0] B,
  input  start,
  input  clear,
  input  clk,
  output busy,
  output [7:0] \output 
);

  wire _00, _01, _10, _11, a_eq_b, a_gt_b, a_lt_b, and_1_out, and_2_out, and_3_out, multiplexer_2_out,
       multiplexer_3_out, not_1_out, or_1_out, or_2_out, or_3_out, Qa, Qb;
  wire [7:0] a_t, b_t, multiplexer_1_out, multiplexer_4_out, multiplexer_5_out, sub_1_s, sub_2_s;

  Decoder #(.Selector_Bits(2)) decoder_1 (.sel({Qa, Qb}), .out_0(_00), .out_1(_01), .out_2(_10), .out_3(_11));
  Sub #(.Bits(8)) sub_1 (.a(a_t), .b(b_t), .c_i(1'b0), .s(sub_1_s));  // open: c_o
  and and_1 (and_1_out, ~a_eq_b, ~a_gt_b);  // And
  not not_1 (not_1_out, a_eq_b);
  Multiplexer #(.Bits(8)) multiplexer_1 (.sel(_10), .in_0(A), .in_1(sub_1_s), .out(multiplexer_1_out));
  Comparator #(.Bits(8)) comparator_1 (.a(a_t), .b(b_t), .gt(a_gt_b), .eq(a_eq_b), .lt(a_lt_b));
  or or_1 (or_1_out, _00, _10);
  Multiplexer #(.Selector_Bits(2)) multiplexer_2 (
    .sel({Qa, Qb}), .in_0(start), .in_1(and_1_out), .in_2(1'b1), .in_3(1'b1), .out(multiplexer_2_out));
  Multiplexer #(.Selector_Bits(2)) multiplexer_3 (
    .sel({Qa, Qb}), .in_0(1'b0), .in_1(not_1_out), .in_2(1'b0), .in_3(1'b0), .out(multiplexer_3_out));
  Register #(.Bits(8)) RegA (.D(multiplexer_1_out), .C(clk), .en(or_1_out), .Q(a_t));
  and and_2 (and_2_out, ~clear, multiplexer_2_out);  // And
  and and_3 (and_3_out, ~clear, multiplexer_3_out);  // And
  not not_2 (busy, _00);
  Multiplexer #(.Bits(8)) multiplexer_4 (.sel(clear), .in_0(b_t), .in_1({8{1'b0}}), .out(multiplexer_4_out));
  Register #(.Bits(8)) RegO (.D(multiplexer_4_out), .C(clk), .en(or_2_out), .Q(\output ));
  or or_2 (or_2_out, _01, clear);
  D_FF d_ff_1 (.D(and_2_out), .C(clk), .Q(Qb));  // open: nQ
  D_FF d_ff_2 (.D(and_3_out), .C(clk), .Q(Qa));  // open: nQ
  Sub #(.Bits(8)) sub_2 (.a(b_t), .b(a_t), .c_i(1'b0), .s(sub_2_s));  // open: c_o
  Multiplexer #(.Bits(8)) multiplexer_5 (.sel(_11), .in_0(B), .in_1(sub_2_s), .out(multiplexer_5_out));
  Seven_Seg_Hex seven_seg_hex_1 (.d(\output [7:4]), .dp(1'b0));
  or or_3 (or_3_out, _00, _11);
  Seven_Seg_Hex seven_seg_hex_2 (.d(\output [3:0]), .dp(1'b0));
  Register #(.Bits(8)) RegB (.D(multiplexer_5_out), .C(clk), .en(or_3_out), .Q(b_t));

  // Other names for the same wires on the sheet: out[7:0] = \output 

  // Notes on the sheet:
  //   clk: Hz: 2
endmodule
